# Fritzing sketch 7segbreakboard (saved by Fritzing 0.7.12b)
breadboards: 1

parts:
  U1 = 74HC595 [package="DIP16 [THT]"]
  U2 = 74HC595 [package="DIP16 [THT]"]
  Q1 = NPN-Transistor [package="TO92 [THT]"]
  Q2 = NPN-Transistor [package="TO92 [THT]"]
  Q3 = NPN-Transistor [package="TO92 [THT]"]
  Q4 = NPN-Transistor [package="TO92 [THT]"]
  J1 = female pin header, 5 pins [form="♀ (female)"]
  DISP = mystery part, 12 pins [chip_label="7 seg"]

nets:
  N1: U1.Q1, DISP.pin7
  N2: U1.Q2, DISP.pin4
  N3: U1.Q3, DISP.pin2
  N4: U1.Q4, DISP.pin1
  N5: U1.Q5, DISP.pin10
  N6: U1.Q6, DISP.pin5
  N7: U1.Q7, DISP.pin3
  GND: U1.GND, U1.OE, U2.GND, U2.OE, Q1.E, Q2.E, Q3.E, Q4.E, J1.pin5
  N8: U1.Q7', U2.DS
  VCC: U1.MR, U1.VCC, U2.MR, U2.VCC, J1.pin1
  N9: U1.SH_CP, U2.SH_CP, J1.pin4
  N10: U1.ST_CP, U2.ST_CP, J1.pin3
  N11: U1.DS, J1.pin2
  N12: U1.Q0, DISP.pin11
  N13: U2.Q1, Q2.B
  N14: U2.Q2, Q3.B
  N15: U2.Q3, Q4.B
  N16: U2.Q0, Q1.B
  N17: Q1.C, DISP.pin12
  N18: Q2.C, DISP.pin9
  N19: Q3.C, DISP.pin8
  N20: Q4.C, DISP.pin6

notes:
  7seg
  v1.2
  Adrien
  Anselme
  display ext
