# Fritzing sketch midi_clock (saved by Fritzing 0.7.12b)
breadboards: 2

parts:
  MIDI_OUT = DIN-5 jack (MIDI) [package=THT]
  RE1 = Rotary Encoder [package=THT]
  IC1 = atmega328 [package=dip]
  R4 = Resistor [tolerance=±5% resistance=220 package=THT]
  DC_IN = 2.1mm DC Barrel Jack
  D1 = Rectifier Diode [part_number=1N4001 package="300 mil [THT]"]
  IC2 = Voltage Regulator - 5V [package="TO220 [THT]"]
  PWR_SEL = Generic male header - 3 pins [package=THT]
  C3 = Electrolytic Capacitor [capacitance=10µF voltage=25V package="100 mil [THT, electrolytic]"]
  D2 = LED - 3mm [color="Green (570nm)" package="3 mm [THT]"]
  R2 = Resistor [tolerance=±5% resistance=1k package=THT]
  JP3A = Generic male header - 2 pins [package=THT]
  JP3B = Generic male header - 2 pins [package=THT]
  JP3C = Generic male header - 2 pins [package=THT]
  R1 = Resistor [tolerance=±5% resistance=10k package=THT]
  C4 = Electrolytic Capacitor [capacitance=100µF voltage=6.3V package="100 mil [THT, electrolytic]"]
  S1 = Pushbutton [package="[THT]"]
  FTDI = male pin header, 6 pins [form="♂ (male)"]
  R3 = Resistor [tolerance=±5% resistance=10k package=THT]
  D3 = LED - 3mm [color="Red (633nm)" package="3 mm [THT]"]
  C5 = Tantalum Capacitor [capacitance=0.1µF package="200 mil [THT, tantalum]"]
  C1 = Tantalum Capacitor [capacitance=0.1µF package="200 mil [THT, tantalum]"]
  C6 = Tantalum Capacitor [capacitance=0.1µF package="200 mil [THT, tantalum]"]
  C2 = Tantalum Capacitor [capacitance=0.1µF package="200 mil [THT, tantalum]"]
  X1 = Crystal [frequency="16 Mhz" package=THT]
  C7 = Ceramic Capacitor [capacitance=22pF package="100 mil [THT, multilayer]"]
  C8 = Ceramic Capacitor [capacitance=22pF package="100 mil [THT, multilayer]"]
  S3 = Pushbutton [package="[THT]"]
  S4 = Pushbutton [package="[THT]"]
  7SEG = mystery part, 16 pins [chip_label=7seg_led]
  U2 = 74HC595 [package="DIP16 [THT]"]
  U1 = 74HC595 [package="DIP16 [THT]"]

nets:
  N1: MIDI_OUT.5, IC1.D1_(TX), FTDI.pin5
  GND: MIDI_OUT.2, RE1.EncoderPinC, IC1.GND, DC_IN.sleeve, IC2.GND, C3.-, D2.cathode, JP3C.pin1, C4.-, S1.Pin_1, S1.Pin_2, FTDI.pin1, FTDI.pin2, D3.cathode, C5.-, C1.-, C2.-, C7.1, C8.0, S3.Pin_1, S3.Pin_2, S4.Pin_1, S4.Pin_2, U2.GND, U2.OE, U1.GND, U1.OE
  N2: MIDI_OUT.4, R4.Pin_0
  N3: RE1.EncoderPinA, IC1.D10_(PWM)
  N4: RE1.EncoderPinB, IC1.D9_(PWM)
  N5: IC1.RESET, JP3C.pin2, R1.Pin_0, S1.Pin_3, S1.Pin_4, C6.-
  N6: IC1.D0_(RX), FTDI.pin4
  N7: IC1.D2, S3.Pin_3, S3.Pin_4
  N8: IC1.D3_(PWM), S4.Pin_3, S4.Pin_4
  dataPin: IC1.D4, U1.DS
  5V: IC1.VCC, IC1.AVCC, R4.Pin_1, PWR_SEL.pin2, R2.Pin_0, JP3A.pin1, R1.Pin_1, C2.+, U2.MR, U2.VCC, U1.MR, U1.VCC
  N9: IC1.XLAT1, X1.pin_0, C7.0
  N10: IC1.XLAT2, X1.pin_1, C8.1
  N11: IC1.D7, U2.ST_CP, U1.ST_CP
  N12: IC1.D8, U2.SH_CP, U1.SH_CP
  N13: IC1.D11_(PWM), JP3B.pin1
  N14: IC1.D12, JP3A.pin2
  N15: IC1.D13, JP3B.pin2, R3.Pin_1
  N16: DC_IN.center, D1.anode
  9V: D1.cathode, IC2.input_voltage, C3.+, C1.+
  N17: IC2.output_voltage, PWR_SEL.pin1, C4.+, C5.+
  USB_5V: PWR_SEL.pin3, FTDI.pin3
  N18: D2.anode, R2.Pin_1
  N19: FTDI.pin6, C6.+
  N20: R3.Pin_0, D3.anode
  N21: 7SEG.pin1, U1.Q1
  N22: 7SEG.pin2, U1.Q2
  N23: 7SEG.pin3, U2.Q7
  N24: 7SEG.pin5, U2.Q6
  N25: 7SEG.pin6, U1.Q3
  N26: 7SEG.pin8, U1.Q4
  N27: 7SEG.pin11, U2.Q5
  N28: 7SEG.pin13, U2.Q4
  N29: 7SEG.pin14, U2.Q3
  N30: 7SEG.pin15, U2.Q2
  N31: 7SEG.pin16, U2.Q1
  N32: U2.DS, U1.Q7'

notes:
  Power supply
  ISCP
  [  ]

custom parts:
  2.1mm DC Barrel Jack: 2.1mm DC Barrel Jack with Thru-Hole Connectors (breadboardable)
